# Fritzing sketch PUM_diagrama (saved by Fritzing 0.9.9b)
breadboards: 1

parts:
  Componente1 = Arduino Uno (Rev3)
  Mod1 = KY-002 Vibration Switch Module [package="Breakout board"]
  Componente2 = 12 NeoPixel Ring [part_number=1643]  # not connected
  Componente4 = 12 NeoPixel Ring [part_number=1643]  # not connected
  Componente5 = InvenSense MPU6050  # not connected
  Componente6 = 24 NeoPixel Ring [part_number=1586]  # not connected
  JACK1 = 2.1mm Barrel Jack with Terminal Block
  BATT1 = LiPoly Battery (1300mAh)
  R2 = Resistor [tolerance=±5% power=0.25 resistance=470 package=THT]
  R3 = Resistor [tolerance=±5% power=0.25 resistance=470 package=THT]
  R4 = Resistor [tolerance=±5% power=0.25 resistance=470 package=THT]

nets:
  N1: Componente1.D9_PWM, Mod1.S
  N2: Componente1.D3_PWM, R2.Pin_0
  N3: Componente1.D5_PWM, R4.Pin_0
  N4: Componente1.D6_PWM, R3.Pin_0
  5V: Componente1.5V, Mod1.Vin
  N5: Componente1.GND, Mod1.-
  N6: JACK1.POS, BATT1.positive
  N7: JACK1.NEG, BATT1.negative

custom parts:
  KY-002 Vibration Switch Module: Arduino Vibration Switch Module KY-002 Keyes allows detection of shock and vibration.
  12 NeoPixel Ring: 12 ultra bright smart LED NeoPixels are arranged in a circle with 1.5" (37mm) outer diameter. The rings are 'chainable' - connect the output pin of one to the input pin of another. Use only one microcontroller pin to control as many as you can chain together! Each LED is addressable as the driver chip is inside the LED. Each one has ~18mA constant current drive so the color will be very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
  24 NeoPixel Ring: 24 ultra bright smart LED NeoPixels are arranged in a circle with 2.6" (66mm) outer diameter. The rings are 'chainable' - connect the output pin of one to the input pin of another. Use only one microcontroller pin to control as many as you can chain together! Each LED is addressable as the driver chip is inside the LED. Each one has ~18mA constant current drive so the color will be very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
  LiPoly Battery (1300mAh): Lithium Ion Polymer Battery (1300mAh)
